# Fritzing sketch Circuit Diagram (saved by Fritzing 0.9.3b)

parts:
  Mod1 = Raspberry Pi 4B
  IC1 = Rasberry Pi NIOR Camera [chip_label=IC package="DIP (Dual Inline) [THT]"]  # not connected
  PWM1 = PCA9685 16x12-bit PWM Breakout
  BAT1 = Battery Holders [package=lipo-1100mAh]
  BAT2 = Battery Holders [package=lipo-1100mAh]
  BAT3 = Battery Holders [package=lipo-1100mAh]
  U1 = LM2596 step down module
  J1 = Basic Servo
  J3 = Basic Servo
  J2 = Basic Servo

nets:
  N1: Mod1.3V3, PWM1.no_name_yet#505
  N2: Mod1.GPIO2, PWM1.no_name_yet#504
  N3: Mod1.GPIO3, Mod1.GPIO4, PWM1.no_name_yet#503
  N4: Mod1.GND, Mod1.GPIO14, PWM1.no_name_yet#501, PWM1.no_name_yet#701, PWM1.no_name_yet#1000, PWM1.no_name_yet#1004, PWM1.no_name_yet#1008, BAT3.-, U1.IN-, U1.OUT-
  N5: PWM1.no_name_yet#0, J1.pulse
  N6: PWM1.no_name_yet#4, J2.pulse
  N7: PWM1.no_name_yet#8, J3.pulse
  N8: PWM1.no_name_yet#100, PWM1.no_name_yet#104, PWM1.no_name_yet#108, PWM1.no_name_yet#706, U1.OUT+
  N9: BAT1.+, U1.IN+
  N10: BAT1.-, BAT2.+
  N11: BAT2.-, BAT3.+

custom parts:
  Rasberry Pi NIOR Camera: Camera
  LM2596 step down module: LM2596 DC-DC step down power supply module 3 A.
